# Fritzing sketch Layout (saved by Fritzing 0.9.4)

parts:
  Composant1 = Arduino Nano (Rev3.0)
  Composant2 = Barometric Pressure Sensor - BMP180 Breakout (GY-68)
  S2 = Momentary Switch [package=ksa_sealed_tac_switch]
  RGB_SMD_LED1 = SMD RGB LED (WS2812) [package=5050]
  Bauteil1 = Triple Axis Accelerometer Breakout - ADXL335

nets:
  GND: Composant1.GND, Composant2.GND, S2.1, Bauteil1.GND
  N1: Composant1.D6, RGB_SMD_LED1.DIn
  N2: Composant1.D12/MISO, S2.2
  5V: Composant1.5V, Bauteil1.VCC
  N3: Composant1.A5, Composant2.SCL
  N4: Composant1.A4, Composant2.SDA
  N5: Composant1.A1, Bauteil1.ZOUT
  3V3: Composant1.3V3, Composant2.VCC

notes:
  BMP180
  A4 => SDA, A5 => SCL
  Min / Max reset button
  GND + D12
  "NeoPixel" (or similar)
  addressable RGBW LED
  GND => GND
  5V => VCC
  Data In => D6
  ADXL***
  Analog accelerometer
  Z => A1
  rev2
  OR
  rev2b
